// Logisim project branch-comp.circ as structural Verilog: 1 circuit, main circuit branch_comp
module branch_comp (
  input  [31:0] BrData1,
  input  [31:0] BrData2,
  input  BrUn,
  output BrEq,
  output BrLt
);

  wire comparator_1_eq, comparator_1_lt, comparator_2_eq, comparator_2_lt;
  wire [31:0] undriven, undriven_2;

  Multiplexer #(.enable("false"), .width(32)) multiplexer_1 (
    .in0(32'h80000000), .in1({32{1'b0}}), .sel(BrUn));  // open: out
  // XOR_Gate xor_1 has open pins: in0=BrData1, in1=undriven, out=open
  // XOR_Gate xor_2 has open pins: in0=BrData2, in1=undriven_2, out=open
  Comparator #(.width(32)) comparator_1 (
    .a(BrData1), .b(BrData2), .eq(comparator_1_eq), .lt(comparator_1_lt));  // open: gt
  Comparator #(.mode("unsigned"), .width(32)) comparator_2 (
    .a(BrData1), .b(BrData2), .eq(comparator_2_eq), .lt(comparator_2_lt));  // open: gt
  Multiplexer #(.enable("false")) multiplexer_2 (.in0(comparator_1_eq), .in1(comparator_2_eq), .out(BrEq), .sel(BrUn));
  Multiplexer #(.enable("false")) multiplexer_3 (.in0(comparator_1_lt), .in1(comparator_2_lt), .out(BrLt), .sel(BrUn));

  // Notes on the sheet:
  //   INPUTS to your circuit
  //   DON'T CHANGE THE LOCATIONS OF THE INPUTS AND OUTPUTS!
  //   OUTPUT from your circuit
endmodule
