// Logisim project control-logic.circ as structural Verilog: 1 circuit, main circuit control_logic
module control_logic (
  input  [31:0] Instruction,
  input  BrEq,
  input  BrLt,
  output PCSel,
  output RegWEn,
  output [2:0] ImmSel,
  output BrUn,
  output ASel,
  output BSel,
  output [3:0] ALUSel,
  output MemWEn,
  output [1:0] WBSel
);

  wire and_1_out, and_2_out, and_3_out, and_4_out, and_6_out, and_7_out, demultiplexer_1_out0,
       demultiplexer_1_out1, demultiplexer_1_out2, demultiplexer_1_out3, Minus1_out, Minus2_out,
       multiplexer_3_out, not_1_out, not_2_out, not_3_out, not_4_out, not_5_out, not_6_out, not_7_out,
       not_8_out, not_9_out, not_10_out, oneonezero, or_1_out, or_2_out, or_3_out, or_4_out, Plus1_out,
       Plus2_out, Plus4_out, xor_1_out, xor_2_out;
  wire [0:0] and_5_out;
  wire [1:0] priority_encoder_1_out, priority_encoder_2_out;
  wire [2:0] priority_encoder_3_out;
  wire [5:0] adder_1_out, adder_2_out, adder_3_out, adder_4_out, FinalPos, multiplexer_1_out,
       multiplexer_2_out, multiplexer_5_out, ROMInput, subtractor_1_out;
  wire [15:14] rom_1_data;

  Demultiplexer #(.enable("false"), .select(3)) demultiplexer_1 (
    .out0(demultiplexer_1_out0), .out1(demultiplexer_1_out1), .out2(demultiplexer_1_out2),
    .out3(demultiplexer_1_out3), .out6(oneonezero), .in(1'b1), .sel(Instruction[6:4]));  // open: out4, out5, out7
  not not_1 (not_1_out, Instruction[3]);
  not not_2 (not_2_out, Instruction[2]);
  not not_3 (not_3_out, Instruction[14]);
  not not_4 (not_4_out, Instruction[13]);
  and and_1 (and_1_out, oneonezero, not_1_out, not_2_out);
  ROM #(.addrWidth(6), .dataWidth(16)) rom_1 (
    .addr(ROMInput), .data({rom_1_data, WBSel, MemWEn, ALUSel, BSel, ASel, BrUn, ImmSel, RegWEn}));
  and and_2 (and_2_out, not_3_out, not_4_out, Instruction[25]);
  not not_5 (not_5_out, Instruction[12]);
  not not_6 (not_6_out, Instruction[14]);
  or or_1 (or_1_out, demultiplexer_1_out3, demultiplexer_1_out1);
  not not_7 (not_7_out, Instruction[13]);
  not not_8 (not_8_out, Instruction[12]);
  not not_9 (not_9_out, Instruction[30]);
  and and_3 (and_3_out, Instruction[13], not_5_out);
  or or_2 (or_2_out, Instruction[12], Instruction[30]);
  and Plus1 (Plus1_out, demultiplexer_1_out3, and_2_out);
  or or_3 (or_3_out, not_8_out, not_9_out);
  and Minus2 (Minus2_out, Instruction[14], and_1_out);
  Adder #(.width(6)) adder_1 (.a({3'b000, Instruction[14:12]}), .b(6'b000010), .out(adder_1_out));  // open: cin, cout
  or or_4 (or_4_out, Instruction[14], and_3_out);
  and and_4 (and_4_out, not_6_out, or_2_out);
  and Minus1 (Minus1_out, or_1_out, Instruction[14], not_7_out, or_3_out);
  Adder #(.width(6)) adder_2 (.a(adder_1_out), .b(6'b000010), .out(adder_2_out));  // open: cin, cout
  and Plus4 (Plus4_out, demultiplexer_1_out3, or_4_out);
  and Plus2 (Plus2_out, demultiplexer_1_out3, and_4_out);
  not not_10 (not_10_out, Instruction[3]);
  Subtractor #(.width(6)) subtractor_1 (
    .a(multiplexer_1_out), .b(6'b000010), .out(subtractor_1_out));  // open: bin, bout
  Priority_Encoder #(.select(2)) priority_encoder_1 (
    .in0(1'b1), .in1(Plus4_out), .in2(Plus2_out), .out(priority_encoder_1_out));  // open: in3, gs, en_out, en_in
  Multiplexer #(.enable("false"), .select(2), .width(6)) multiplexer_1 (
    .in0({3'b000, Instruction[14:12]}), .in1(adder_2_out), .in2(adder_1_out), .out(multiplexer_1_out),
    .sel(priority_encoder_1_out));  // open: in3
  Adder #(.width(6)) adder_3 (.a(subtractor_1_out), .b(6'b000001), .out(adder_3_out));  // open: cin, cout
  Priority_Encoder #(.select(2)) priority_encoder_2 (
    .in0(1'b1), .in1(Plus1_out), .in2(Minus1_out), .in3(Minus2_out), .out(priority_encoder_2_out));  // open: gs, en_out, en_in
  Adder #(.width(6)) adder_4 (.a(adder_3_out), .b(6'b000010), .out(adder_4_out));  // open: cin, cout
  and and_5 (and_5_out[0], Instruction[5], not_10_out);
  xor xor_1 (xor_1_out, BrEq, Instruction[12]);
  xor xor_2 (xor_2_out, Instruction[12], BrLt);
  Multiplexer #(.enable("false"), .select(2), .width(6)) multiplexer_2 (
    .in0(multiplexer_1_out), .in1(adder_4_out), .in2(adder_3_out), .in3(subtractor_1_out),
    .out(multiplexer_2_out), .sel(priority_encoder_2_out));
  Multiplexer #(.enable("false")) multiplexer_3 (
    .in0(xor_1_out), .in1(xor_2_out), .out(multiplexer_3_out), .sel(Instruction[14]));
  Multiplexer #(.enable("false"), .width(6)) multiplexer_4 (
    .in0(multiplexer_2_out), .in1({4'b0000, Instruction[6], and_5_out[0]}), .out(FinalPos),
    .sel(Instruction[2]));
  and and_6 (and_6_out, and_1_out, multiplexer_3_out);
  and and_7 (and_7_out, Instruction[6], Instruction[2]);
  Multiplexer #(.enable("false"), .select(3), .width(6)) multiplexer_5 (
    .in0({6{1'b0}}), .in1(6'b001100), .in2(6'b001111), .in3(6'b010111), .in4(6'b011010), .in5(6'b100000),
    .out(multiplexer_5_out), .sel(priority_encoder_3_out));  // open: in6, in7
  Priority_Encoder priority_encoder_3 (
    .in0(demultiplexer_1_out3), .in1(demultiplexer_1_out0), .in2(demultiplexer_1_out1),
    .in3(demultiplexer_1_out2), .in4(and_1_out), .in5(Instruction[2]), .out(priority_encoder_3_out));  // open: in6, in7, en_in, gs, en_out
  or or_5 (PCSel, and_6_out, and_7_out);
  Adder #(.width(6)) adder_5 (.a(multiplexer_5_out), .b(FinalPos), .out(ROMInput));  // open: cin, cout

  // Other names for the same wires on the sheet: Opcode[6:0] = Instruction[6:0]; Funct77thDig = Instruction[25];
  //   Funct72ndDig = Instruction[30]; Funct3[2:0] = Instruction[14:12]; Position[2:0] = Instruction[14:12]

  // Notes on the sheet:
  //   INPUTS to your circuit
  //   Connect ROM Input here ->
  //   contents of rom_1 (hex, n*v repeats v):
  //   1001 1401 1601 1081 1481 1581 1101 1201 1281 1681 1301 1381 41 41 41 1041 10c1 1141 1241 12c1 16c1
  //   1341 13c1 842 842 842 4*64 74 74 1067 17e7 2069 2045
  //   ROM FOR CONTROL LOGIC
  //   DON'T CHANGE THE LOCATIONS OF THE INPUTS AND OUTPUTS!
  //   This is only if you choose to do the ROM option
  //   CONNECT
  //   WIRE
  //   TO
  //   USE
  //   ROM
  //   OUTPUT from your circuit
  //   Reminder: If using ROM, use combinational logic for PCSel
endmodule
