// Logisim project cpu.circ as structural Verilog: 1 circuit, main circuit cpu
module cpu (
  input  clk,
  input  [31:0] Instruction,
  input  [31:0] MemReadData,
  output [31:0] MemAddress,
  output [31:0] ProgramCounter,
  output [31:0] ra,
  output [31:0] sp,
  output [31:0] t0,
  output [31:0] t1,
  output [31:0] t2,
  output [31:0] s0,
  output [31:0] s1,
  output [31:0] a0,
  output [3:0] MemWriteMask,
  output [31:0] MemWriteData
);

  wire BrEq, BrLt, BrUn, control_logic_1_asel, control_logic_1_bsel, control_logic_1_regwen, MemWEn, PCsel,
       register_1_q, undriven;
  wire [1:0] WBSel;
  wire [2:0] control_logic_1_immsel;
  wire [3:0] control_logic_1_alusel;
  wire [31:0] adder_2_out, BrData1, BrData2, imm_gen_1_immediate, Instruction_2, Instruction_2_q,
       multiplexer_1_out, multiplexer_3_out, multiplexer_4_out, partial_load_1_datatoreg, PC_2, PCPlus4,
       RegWriteData;

  Register #(.width(32)) u_Instruction_2 (.D(Instruction), .clk(clk), .Q(Instruction_2_q));  // open: en, clr
  Multiplexer #(.enable("false"), .width(32)) multiplexer_1 (
    .in0(PCPlus4), .in1(MemAddress), .out(multiplexer_1_out), .sel(PCsel));
  Register #(.width(32)) PC (.D(multiplexer_1_out), .clk(clk), .Q(ProgramCounter));  // open: en, clr
  Adder #(.width(32)) adder_1 (.a(ProgramCounter), .b(32'h4), .out(PCPlus4));  // open: cin, cout
  Multiplexer #(.enable("false"), .width(32)) multiplexer_2 (
    .in0(Instruction_2_q), .in1(32'h13), .out(Instruction_2), .sel(register_1_q));
  Register #(.width(1)) register_1 (.D(PCsel), .clk(clk), .Q(register_1_q), .clr(undriven));  // open: en
  Register #(.width(32)) register_2 (.D(ProgramCounter), .clk(clk), .Q(PC_2));  // open: en, clr
  control_logic control_logic_1 (
    .PCSel(PCsel), .RegWEn(control_logic_1_regwen), .ImmSel(control_logic_1_immsel), .BrUn(BrUn),
    .ASel(control_logic_1_asel), .BSel(control_logic_1_bsel), .ALUSel(control_logic_1_alusel),
    .MemWEn(MemWEn), .WBSel(WBSel), .Instruction(Instruction_2), .BrEq(BrEq), .BrLt(BrLt));
  regfile regfile_1 (
    .ReadReg1(Instruction_2[19:15]), .ReadReg2(Instruction_2[24:20]), .WriteReg(Instruction_2[11:7]),
    .RegWriteData(RegWriteData), .RegWEn(control_logic_1_regwen), .clk(clk), .ra(ra), .sp(sp), .t0(t0),
    .t1(t1), .t2(t2), .s0(s0), .s1(s1), .a0(a0), .RegReadData1(BrData1), .RegReadData2(BrData2));
  imm_gen imm_gen_1 (.Instruction(Instruction_2), .ImmSel(control_logic_1_immsel), .Immediate(imm_gen_1_immediate));
  Multiplexer #(.enable("false"), .width(32)) multiplexer_3 (
    .in0(BrData1), .in1(PC_2), .out(multiplexer_3_out), .sel(control_logic_1_asel));
  Multiplexer #(.enable("false"), .width(32)) multiplexer_4 (
    .in0(BrData2), .in1(imm_gen_1_immediate), .out(multiplexer_4_out), .sel(control_logic_1_bsel));
  alu alu_1 (.ALUResult(MemAddress), .A(multiplexer_3_out), .B(multiplexer_4_out), .ALUSel(control_logic_1_alusel));
  branch_comp branch_comp_1 (.BrData1(BrData1), .BrData2(BrData2), .BrUn(BrUn), .BrEq(BrEq), .BrLt(BrLt));
  Adder #(.width(32)) adder_2 (.a(PC_2), .b(32'h4), .out(adder_2_out));  // open: cin, cout
  partial_store partial_store_1 (
    .Instruction(Instruction_2), .MemAddress(MemAddress), .DataFromReg(BrData2), .MemWEn(MemWEn),
    .MemWriteMask(MemWriteMask), .DataToMem(MemWriteData));
  partial_load partial_load_1 (
    .Instruction(Instruction_2), .MemAddress(MemAddress), .DataFromMem(MemReadData),
    .DataToReg(partial_load_1_datatoreg));
  Multiplexer #(.enable("false"), .select(2), .width(32)) multiplexer_5 (
    .in0(partial_load_1_datatoreg), .in1(MemAddress), .in2(adder_2_out), .out(RegWriteData), .sel(WBSel));  // open: in3

  // Notes on the sheet:
  //   To IMEM
  //   IMEM (do **NOT** move this)
  //   From IMEM
  //   Inputs/Outputs for testing. Do **NOT** move these.
  //   It is OK to move the PC, RegFile, ALU, MEM, Branch Comp, Imm Gen, Partial Load, Partial Store and Control Logic to wherever is most convenient for you when constructing your CPU, and to delete this text
  //   To DMEM
  //   DMEM (do **NOT** move this)
  //   From DMEM
endmodule
