// Logisim project regfile.circ as structural Verilog: 1 circuit, main circuit regfile
module regfile (
  input  [4:0] ReadReg1,
  input  [4:0] ReadReg2,
  input  [4:0] WriteReg,
  input  [31:0] RegWriteData,
  input  RegWEn,
  input  clk,
  output [31:0] ra,
  output [31:0] sp,
  output [31:0] t0,
  output [31:0] t1,
  output [31:0] t2,
  output [31:0] s0,
  output [31:0] s1,
  output [31:0] a0,
  output [31:0] RegReadData1,
  output [31:0] RegReadData2
);

  wire demultiplexer_1_out1, demultiplexer_1_out2, demultiplexer_1_out3, demultiplexer_1_out4,
       demultiplexer_1_out5, demultiplexer_1_out6, demultiplexer_1_out7, demultiplexer_1_out8,
       demultiplexer_1_out9, demultiplexer_1_out10, demultiplexer_1_out11, demultiplexer_1_out12,
       demultiplexer_1_out13, demultiplexer_1_out14, demultiplexer_1_out15, demultiplexer_1_out16,
       demultiplexer_1_out17, demultiplexer_1_out18, demultiplexer_1_out19, demultiplexer_1_out20,
       demultiplexer_1_out21, demultiplexer_1_out22, demultiplexer_1_out23, demultiplexer_1_out24,
       demultiplexer_1_out25, demultiplexer_1_out26, demultiplexer_1_out27, demultiplexer_1_out28,
       demultiplexer_1_out29, demultiplexer_1_out30, demultiplexer_1_out31;
  wire [31:0] x0, x3, x4, x11, x12, x13, x14, x15, x16, x17, x18, x19, x20, x21, x22, x23, x24, x25, x26,
       x27, x28, x29, x30, x31;

  Demultiplexer #(.enable("false"), .select(5)) demultiplexer_1 (
    .out1(demultiplexer_1_out1), .out2(demultiplexer_1_out2), .out3(demultiplexer_1_out3),
    .out4(demultiplexer_1_out4), .out5(demultiplexer_1_out5), .out6(demultiplexer_1_out6),
    .out7(demultiplexer_1_out7), .out8(demultiplexer_1_out8), .out9(demultiplexer_1_out9),
    .out10(demultiplexer_1_out10), .out11(demultiplexer_1_out11), .out12(demultiplexer_1_out12),
    .out13(demultiplexer_1_out13), .out14(demultiplexer_1_out14), .out15(demultiplexer_1_out15),
    .out16(demultiplexer_1_out16), .out17(demultiplexer_1_out17), .out18(demultiplexer_1_out18),
    .out19(demultiplexer_1_out19), .out20(demultiplexer_1_out20), .out21(demultiplexer_1_out21),
    .out22(demultiplexer_1_out22), .out23(demultiplexer_1_out23), .out24(demultiplexer_1_out24),
    .out25(demultiplexer_1_out25), .out26(demultiplexer_1_out26), .out27(demultiplexer_1_out27),
    .out28(demultiplexer_1_out28), .out29(demultiplexer_1_out29), .out30(demultiplexer_1_out30),
    .out31(demultiplexer_1_out31), .in(RegWEn), .sel(WriteReg));  // open: out0
  Register #(.width(32)) u_x0 (.D({32{1'b0}}), .clk(clk), .Q(x0));  // open: en, clr
  Register #(.width(32)) x1 (.D(RegWriteData), .en(demultiplexer_1_out1), .clk(clk), .Q(ra));  // open: clr
  Register #(.width(32)) x2 (.D(RegWriteData), .en(demultiplexer_1_out2), .clk(clk), .Q(sp));  // open: clr
  Register #(.width(32)) u_x3 (.D(RegWriteData), .en(demultiplexer_1_out3), .clk(clk), .Q(x3));  // open: clr
  Register #(.width(32)) u_x4 (.D(RegWriteData), .en(demultiplexer_1_out4), .clk(clk), .Q(x4));  // open: clr
  Register #(.width(32)) x5 (.D(RegWriteData), .en(demultiplexer_1_out5), .clk(clk), .Q(t0));  // open: clr
  Register #(.width(32)) x6 (.D(RegWriteData), .en(demultiplexer_1_out6), .clk(clk), .Q(t1));  // open: clr
  Register #(.width(32)) x7 (.D(RegWriteData), .en(demultiplexer_1_out7), .clk(clk), .Q(t2));  // open: clr
  Register #(.width(32)) x8 (.D(RegWriteData), .en(demultiplexer_1_out8), .clk(clk), .Q(s0));  // open: clr
  Register #(.width(32)) x9 (.D(RegWriteData), .en(demultiplexer_1_out9), .clk(clk), .Q(s1));  // open: clr
  Register #(.width(32)) x10 (.D(RegWriteData), .en(demultiplexer_1_out10), .clk(clk), .Q(a0));  // open: clr
  Register #(.width(32)) u_x11 (.D(RegWriteData), .en(demultiplexer_1_out11), .clk(clk), .Q(x11));  // open: clr
  Register #(.width(32)) u_x12 (.D(RegWriteData), .en(demultiplexer_1_out12), .clk(clk), .Q(x12));  // open: clr
  Register #(.width(32)) u_x13 (.D(RegWriteData), .en(demultiplexer_1_out13), .clk(clk), .Q(x13));  // open: clr
  Register #(.width(32)) u_x14 (.D(RegWriteData), .en(demultiplexer_1_out14), .clk(clk), .Q(x14));  // open: clr
  Register #(.width(32)) u_x15 (.D(RegWriteData), .en(demultiplexer_1_out15), .clk(clk), .Q(x15));  // open: clr
  Register #(.width(32)) u_x16 (.D(RegWriteData), .en(demultiplexer_1_out16), .clk(clk), .Q(x16));  // open: clr
  Register #(.width(32)) u_x17 (.D(RegWriteData), .en(demultiplexer_1_out17), .clk(clk), .Q(x17));  // open: clr
  Register #(.width(32)) u_x18 (.D(RegWriteData), .en(demultiplexer_1_out18), .clk(clk), .Q(x18));  // open: clr
  Register #(.width(32)) u_x19 (.D(RegWriteData), .en(demultiplexer_1_out19), .clk(clk), .Q(x19));  // open: clr
  Register #(.width(32)) u_x20 (.D(RegWriteData), .en(demultiplexer_1_out20), .clk(clk), .Q(x20));  // open: clr
  Register #(.width(32)) u_x21 (.D(RegWriteData), .en(demultiplexer_1_out21), .clk(clk), .Q(x21));  // open: clr
  Register #(.width(32)) u_x22 (.D(RegWriteData), .en(demultiplexer_1_out22), .clk(clk), .Q(x22));  // open: clr
  Register #(.width(32)) u_x23 (.D(RegWriteData), .en(demultiplexer_1_out23), .clk(clk), .Q(x23));  // open: clr
  Register #(.width(32)) u_x24 (.D(RegWriteData), .en(demultiplexer_1_out24), .clk(clk), .Q(x24));  // open: clr
  Register #(.width(32)) u_x25 (.D(RegWriteData), .en(demultiplexer_1_out25), .clk(clk), .Q(x25));  // open: clr
  Register #(.width(32)) u_x26 (.D(RegWriteData), .en(demultiplexer_1_out26), .clk(clk), .Q(x26));  // open: clr
  Register #(.width(32)) u_x27 (.D(RegWriteData), .en(demultiplexer_1_out27), .clk(clk), .Q(x27));  // open: clr
  Register #(.width(32)) u_x28 (.D(RegWriteData), .en(demultiplexer_1_out28), .clk(clk), .Q(x28));  // open: clr
  Register #(.width(32)) u_x29 (.D(RegWriteData), .en(demultiplexer_1_out29), .clk(clk), .Q(x29));  // open: clr
  Register #(.width(32)) u_x30 (.D(RegWriteData), .en(demultiplexer_1_out30), .clk(clk), .Q(x30));  // open: clr
  Register #(.width(32)) u_x31 (.D(RegWriteData), .en(demultiplexer_1_out31), .clk(clk), .Q(x31));  // open: clr
  Multiplexer #(.enable("false"), .select(5), .width(32)) multiplexer_1 (
    .in0(x0), .in1(ra), .in2(sp), .in3(x3), .in4(x4), .in5(t0), .in6(t1), .in7(t2), .in8(s0), .in9(s1),
    .in10(a0), .in11(x11), .in12(x12), .in13(x13), .in14(x14), .in15(x15), .in16(x16), .in17(x17),
    .in18(x18), .in19(x19), .in20(x20), .in21(x21), .in22(x22), .in23(x23), .in24(x24), .in25(x25),
    .in26(x26), .in27(x27), .in28(x28), .in29(x29), .in30(x30), .in31(x31), .out(RegReadData1), .sel(ReadReg1));
  Multiplexer #(.enable("false"), .select(5), .width(32)) multiplexer_2 (
    .in0(x0), .in1(ra), .in2(sp), .in3(x3), .in4(x4), .in5(t0), .in6(t1), .in7(t2), .in8(s0), .in9(s1),
    .in10(a0), .in11(x11), .in12(x12), .in13(x13), .in14(x14), .in15(x15), .in16(x16), .in17(x17),
    .in18(x18), .in19(x19), .in20(x20), .in21(x21), .in22(x22), .in23(x23), .in24(x24), .in25(x25),
    .in26(x26), .in27(x27), .in28(x28), .in29(x29), .in30(x30), .in31(x31), .out(RegReadData2), .sel(ReadReg2));

  // Other names for the same wires on the sheet: x1[31:0] = ra; x2[31:0] = sp; x5[31:0] = t0; x6[31:0] = t1;
  //   x7[31:0] = t2; x8[31:0] = s0; x9[31:0] = s1; x10[31:0] = a0

  // Notes on the sheet:
  //   INPUTS to your circuit
  //   DON'T CHANGE THE LOCATIONS OF THE INPUTS AND OUTPUTS!
  //   These are DEBUG/TEST outputs from your circuit.
  //   OUTPUTS from your circuit
endmodule
